// Logisim project 6502.circ as structural Verilog
module PLA (
  input  in_1,
  input  in_2,
  input  in_3,
  input  in_4,
  input  [7:0] IR,
  input  in_6,
  input  in_7,
  output out_8,
  output out_9,
  output out_10,
  output out_11,
  output out_12,
  output out_13,
  output out_14,
  output out_15,
  output out_16,
  output out_17
);

  wire nor_11_out, nor_12_out;

  nor nor_1 (out_8, IR[6], ~IR[2], ~IR[7], IR[5], nor_12_out);  // NOR_Gate
  nor nor_2 (out_9, ~IR[4], ~IR[0], in_3, IR[3], IR[2]);  // NOR_Gate
  nor nor_3 (out_10, ~IR[4], ~IR[0], in_4, ~IR[3], IR[2]);  // NOR_Gate
  nor nor_4 (out_11, in_6, IR[4], ~IR[7], ~IR[3], IR[5], nor_12_out, IR[2]);  // NOR_Gate
  nor nor_5 (out_12, in_6, IR[6], ~IR[7], ~IR[4], ~IR[3], IR[5], nor_12_out, IR[2]);  // NOR_Gate
  nor nor_6 (out_13, in_6, IR[4], ~IR[7], ~IR[6], IR[5], nor_12_out);  // NOR_Gate
  nor nor_7 (out_14, ~IR[2], ~IR[4], in_4);  // NOR_Gate
  nor nor_8 (out_15, IR[6], ~IR[7], ~IR[1]);  // NOR_Gate
  nor nor_9 (out_16, IR[4], ~IR[0], in_4, IR[3], IR[2]);  // NOR_Gate
  nor nor_10 (out_17, in_6, IR[6], IR[4], ~IR[7], ~IR[1], ~IR[3], IR[5], IR[2]);  // NOR_Gate
  nor nor_11 (nor_11_out, in_6, IR[4]);
  nor nor_12 (nor_12_out, IR[0], IR[1]);
endmodule
